# Fritzing sketch DHT11_with_18B20_Temp_V2 (saved by Fritzing 0.9.3b)
circuit board: 12cm x 6cm
circuit board: 7cm x 1.5cm
breadboards: 1

parts:
  R1 = Trimmer Potentiometer [maximum_resistance=5kΩ package=THT]
  R2 = Trimmer Potentiometer [maximum_resistance=5kΩ package=THT]
  LED3 = LED - 5mm [color="Green (555nm)" package="5 mm [THT]"]
  LED4 = LED - 5mm [color="Red (633nm)" package="5 mm [THT]"]
  LED5 = LED - 5mm [color="Yellow (592nm)" package="5 mm [THT]"]
  R3 = Resistor [tolerance=±5% resistance=330 package=THT]
  R4 = Resistor [tolerance=±5% resistance=330 package=THT]
  R5 = Resistor [tolerance=±5% resistance=330 package=THT]
  Part2 = KY-015 Temperature & Humidity Sensor Module [package="Breakout board"]
  Part3 = KY-001 Temperature Sensor Module [package="Breakout board"]
  Part1 = Arduino Mega 2560 (Rev3)
  LCD1 = LCD screen

nets:
  GND: R1.leg1, R2.leg1, LED3.cathode, LED4.cathode, LED5.cathode, Part2.-, Part3.-, Part1.GND, LCD1.VSS, LCD1.R/W, LCD1.LED-
  N1: R1.wiper, LCD1.V0
  VIN: R1.leg2, R2.leg2, Part2.Vin, Part3.Vin, Part1.5V, LCD1.VDD
  N2: R2.wiper, LCD1.LED+
  N3: LED3.anode, R3.Pin_1
  N4: LED4.anode, R5.Pin_1
  N5: LED5.anode, R4.Pin_1
  N6: R3.Pin_0, Part1.D8_PWM
  N7: R4.Pin_0, Part1.D9_PWM
  N8: R5.Pin_0, Part1.D10_PWM
  N9: Part2.S, Part1.A0
  N10: Part3.S, Part1.D12_PWM
  N11: Part1.D2_PWM, LCD1.DB7
  N12: Part1.D3_PWM, LCD1.DB6
  N13: Part1.D4_PWM, LCD1.DB5
  N14: Part1.D5_PWM, LCD1.DB4
  N15: Part1.D6_PWM, LCD1.E
  N16: Part1.D7_PWM, LCD1.RS

custom parts:
  KY-015 Temperature & Humidity Sensor Module: KY-015 temperature and humidity sensor module, provides a low-latency serial interface to measure humidity and temperature.
  KY-001 Temperature Sensor Module: Arduino Temperature Sensor Module Keyes KY-001, Allows ambient temperature measurement using digital serial bus (DS18B20)
