# Fritzing sketch DHT11_with_2x_18B20_Temp_nano (saved by Fritzing 0.9.3b)
circuit board: 10cm x 10cm
breadboards: 1

parts:
  R2 = Trimmer Potentiometer [maximum_resistance=5kΩ package=THT]
  R3 = Resistor [tolerance=±5% resistance=330 package=THT]
  LED4 = LED - 5mm [color="Red (633nm)" package="5 mm [THT]"]
  LCD1 = LCD screen
  Part3 = KY-001 Temperature Sensor Module [package="Breakout board"]
  Part2 = KY-015 Temperature & Humidity Sensor Module [package="Breakout board"]
  R1 = Trimmer Potentiometer [maximum_resistance=5kΩ package=THT]
  R5 = Resistor [tolerance=±5% resistance=330 package=THT]
  R4 = Resistor [tolerance=±5% resistance=330 package=THT]
  LED5 = LED - 5mm [color="Yellow (592nm)" package="5 mm [THT]"]
  Part4 = Arduino Nano (Rev3.0)
  LED3 = LED - 5mm [color="Green (555nm)" package="5 mm [THT]"]
  J1 = Power Jack [package=power_jack_combo]

nets:
  GND: R2.leg1, LED4.cathode, LCD1.VSS, LCD1.R/W, LCD1.LED-, Part3.-, Part2.-, R1.leg1, LED5.cathode, Part4.GND, LED3.cathode, J1.GND, J1.GNDBREAK
  N1: R2.wiper, LCD1.LED+
  VIN: R2.leg2, LCD1.VDD, Part3.Vin, Part2.Vin, R1.leg2, Part4.5V
  N2: R3.Pin_0, Part4.D10
  N3: R3.Pin_1, LED3.anode
  N4: LED4.anode, R5.Pin_1
  N5: LCD1.V0, R1.wiper
  N6: LCD1.RS, Part4.D9
  N7: LCD1.E, Part4.D8
  N8: LCD1.DB4, Part4.D5
  N9: LCD1.DB5, Part4.D4
  N10: LCD1.DB6, Part4.D3
  N11: LCD1.DB7, Part4.D2
  N12: Part3.S, Part4.D6
  N13: Part2.S, Part4.A5
  N14: R5.Pin_0, Part4.D12/MISO
  N15: R4.Pin_0, Part4.D11/MOSI
  N16: R4.Pin_1, LED5.anode
  N17: Part4.VIN, J1.PWR

custom parts:
  KY-001 Temperature Sensor Module: Arduino Temperature Sensor Module Keyes KY-001, Allows ambient temperature measurement using digital serial bus (DS18B20)
  KY-015 Temperature & Humidity Sensor Module: KY-015 temperature and humidity sensor module, provides a low-latency serial interface to measure humidity and temperature.
